# Fritzing sketch code-cracker (saved by Fritzing 0.9.3b)
breadboards: 1

parts:
  Raspberry_Pi1 = Raspberry Pi B rev2
  S2 = Round Pushbutton
  S3 = Round Pushbutton
  S4 = Round Pushbutton
  S5 = Round Pushbutton
  LED3 = LED - 3mm [color="Blue (525nm)" package="3 mm [THT]"]
  LED4 = LED - 3mm [color="Green (570nm)" package="3 mm [THT]"]
  LED2 = LED - 3mm [color="Orange (620nm)" package="3 mm [THT]"]
  LED1 = LED - 3mm [color="Red (633nm)" package="3 mm [THT]"]
  R1 = Resistor [tolerance=±5% resistance=270 package="0805 [SMD]"]
  R2 = Resistor [tolerance=±5% resistance=270 package="0805 [SMD]"]
  R3 = Resistor [tolerance=±5% resistance=270 package="0805 [SMD]"]
  R4 = Resistor [tolerance=±5% resistance=1k package="0805 [SMD]"]

nets:
  N1: Raspberry_Pi1.3V3, S2.leg1, S3.leg1, S4.leg1, S5.leg1
  N2: Raspberry_Pi1.GND, R1.Pin_0, R2.Pin_0, R3.Pin_0, R4.Pin_0
  N3: Raspberry_Pi1.GPIO_23, S2.leg0
  N4: Raspberry_Pi1.GPIO_22, LED3.anode
  N5: Raspberry_Pi1.GPIO_24, S3.leg0
  N6: Raspberry_Pi1.GPIO_10, LED2.anode
  N7: Raspberry_Pi1.GPIO_9, LED4.anode
  N8: Raspberry_Pi1.GPIO_25, S4.leg0
  N9: Raspberry_Pi1.GPIO_11, LED1.anode
  N10: Raspberry_Pi1.GPIO_8, S5.leg0
  N11: LED3.cathode, R4.Pin_1
  N12: LED4.cathode, R3.Pin_1
  N13: LED2.cathode, R1.Pin_1
  N14: LED1.cathode, R2.Pin_1
